# Fritzing sketch remote-control-joystick (saved by Fritzing 0.9.3b)
breadboards: 1

parts:
  Arduino-Nano = Arduino Nano (Rev3.0)
  NRF24L01 = NRF24L01+ Breakout Board
  Joystick1 = Thumb Joystick [package=joystick]
  Raspberry_Pi_1 = Raspberry Pi 3 [part_number=RPI-3-V1.2]  # not connected

nets:
  GND: Arduino-Nano.GND, NRF24L01.GND, Joystick1.GND
  N1: Arduino-Nano.D2, Joystick1.SW
  N2: Arduino-Nano.D7, NRF24L01.CE
  N3: Arduino-Nano.D8, NRF24L01.CS
  N4: Arduino-Nano.D11/MOSI, NRF24L01.SCK
  N5: Arduino-Nano.D12/MISO, NRF24L01.MISO
  N6: Arduino-Nano.VIN, Joystick1.V+
  N7: Arduino-Nano.A1, Joystick1.VRx
  N8: Arduino-Nano.A0, Joystick1.VRy
  3V3: Arduino-Nano.3V3, NRF24L01.VCC
  N9: Arduino-Nano.D13/SCK, NRF24L01.MOSI

custom parts:
  Thumb Joystick: Thumb Joystick from OSEPP, two potentiometers for verticle and horizontal. It also has a push button switch.
